# Fritzing sketch PiezoServo12 (saved by Fritzing 0.9.2b)
circuit board: 3.03975cm x 3.66426cm
breadboards: 1

parts:
  J1 = Basic Servo
  Part2 = Arduino Pro Mini v13
  Piezo_element = Piezo Speaker
  part = Resistor [tolerance=±5% resistance=1M package=THT]
  12V_power = Power plug

nets:
  GND: J1.gnd, Part2.GND, Piezo_element.pin1, part.Pin_1, 12V_power.GND
  VCC: J1.vcc, Part2.VCC
  N1: J1.pulse, Part2.D3_PWM
  N2: Part2.RAW, 12V_power.VCC
  N3: Part2.A0, Piezo_element.pin2, part.Pin_0
